// Logisim project CPU.circ as structural Verilog: 5 circuits, main circuit main
module main (
  input  in_1,
  input  in_2,
  output [15:0] out_3
);

  wire alu_1_out_5, and_1_out, and_2_out, and_3_out, clock_1_out, control_unit_1_alusrc,
       control_unit_1_branch, control_unit_1_enjump, control_unit_1_enreboot, control_unit_1_li,
       control_unit_1_memread, control_unit_1_memtoreg, control_unit_1_memwrite, control_unit_1_read_ra,
       control_unit_1_regdst, control_unit_1_regwrite, control_unit_1_write_ra, not_1_out, or_1_out;
  wire [2:0] bit_extender_1_out, multiplexer_1_out;
  wire [3:0] alucontrol_1_u;
  wire [4:0] rom_1_data_2;
  wire [10:0] rom_1_data;
  wire [15:0] adder_1_out, adder_2_out, alu_1_aluresult, multiplexer_2_out, multiplexer_3_out,
       multiplexer_4_out, multiplexer_5_out, multiplexer_6_out, ra_q, ram_1_data, register_1_q,
       register_file_1_read_data_1, register_file_1_read_data_2;

  Clock clock_1 (.out(clock_1_out));
  ROM #(.addrWidth(16), .dataWidth(16)) rom_1 (.addr(register_1_q), .data({rom_1_data_2, rom_1_data}), .sel(1'b1));
  and and_1 (and_1_out, clock_1_out, control_unit_1_li);
  ALUControl alucontrol_1 (
    .a(rom_1_data_2[4]), .b(rom_1_data_2[3]), .c(rom_1_data_2[2]), .d(rom_1_data_2[1]), .e(rom_1_data_2[0]),
    .x(alucontrol_1_u[3]), .y(alucontrol_1_u[2]), .z(alucontrol_1_u[1]), .u(alucontrol_1_u[0]));
  Register #(.width(16)) register_1 (
    .D(multiplexer_4_out), .en(control_unit_1_li), .Q(register_1_q), .clk(clock_1_out));  // open: clr
  Control_Unit control_unit_1 (
    .a(rom_1_data_2[4]), .b(rom_1_data_2[3]), .c(rom_1_data_2[2]), .d(rom_1_data_2[1]), .e(rom_1_data_2[0]),
    .RegDst(control_unit_1_regdst), .RegWrite(control_unit_1_regwrite), .ALUSrc(control_unit_1_alusrc),
    .Branch(control_unit_1_branch), .MemRead(control_unit_1_memread), .MemWrite(control_unit_1_memwrite),
    .MemtoReg(control_unit_1_memtoreg), .Li(control_unit_1_li), .Write_ra(control_unit_1_write_ra),
    .Read_ra(control_unit_1_read_ra), .EnReboot(control_unit_1_enreboot), .Enjump(control_unit_1_enjump));
  Bit_Extender #(.in_width(5), .out_width(3), .\type ("sign")) bit_extender_1 (
    .in(rom_1_data[4:0]), .out(bit_extender_1_out));
  Multiplexer #(.width(3), .enable("false")) multiplexer_1 (
    .in0(rom_1_data[7:5]), .in1(bit_extender_1_out), .out(multiplexer_1_out), .sel(control_unit_1_regdst));
  register_file register_file_1 (
    .Read_Register_1(rom_1_data[10:8]), .Read_Register_2(rom_1_data[7:5]),
    .Write_Rigister(multiplexer_1_out), .Write_Data(multiplexer_6_out), .Write(control_unit_1_regwrite),
    .Clock(and_1_out), .Reset(in_1), .Read_Data_1(register_file_1_read_data_1),
    .Read_Data_2(register_file_1_read_data_2));
  assign out_3 = {{11{rom_1_data[4]}}, rom_1_data[4:0]};  // Bit_Extender bit_extender_2
  Multiplexer #(.width(16), .enable("false")) multiplexer_2 (
    .in0(register_file_1_read_data_2), .in1(out_3), .out(multiplexer_2_out), .sel(control_unit_1_alusrc));
  Adder #(.width(16)) adder_1 (.a(register_1_q), .b(out_3), .out(adder_1_out));  // open: cin, cout
  and and_2 (and_2_out, control_unit_1_write_ra, control_unit_1_li);
  ALU alu_1 (
    .ReadData1(register_file_1_read_data_1), .ReadData2(multiplexer_2_out), .ALUControl(alucontrol_1_u),
    .ALUresult(alu_1_aluresult), .out_5(alu_1_out_5));
  and and_3 (and_3_out, control_unit_1_branch, alu_1_out_5);
  Adder #(.width(16)) adder_2 (.a(16'h1), .b(register_1_q), .out(adder_2_out));  // open: cin, cout
  Multiplexer #(.width(16), .enable("false")) multiplexer_3 (
    .in0(adder_2_out), .in1(adder_1_out), .out(multiplexer_3_out), .sel(or_1_out));
  or or_1 (or_1_out, and_3_out, control_unit_1_enjump);
  not not_1 (not_1_out, clock_1_out);
  Multiplexer #(.width(16), .enable("false")) multiplexer_4 (
    .in0(multiplexer_5_out), .in1({16{1'b0}}), .out(multiplexer_4_out), .sel(control_unit_1_enreboot));
  Multiplexer #(.width(16), .enable("false")) multiplexer_5 (
    .in0(multiplexer_3_out), .in1(ra_q), .out(multiplexer_5_out), .sel(control_unit_1_read_ra));
  Register #(.width(16)) ra (.D(adder_2_out), .en(and_2_out), .Q(ra_q), .clk(clock_1_out));  // open: clr
  RAM #(.addrWidth(16), .dataWidth(16), .bus("separate")) ram_1 (
    .addr(alu_1_aluresult), .din(multiplexer_2_out), .data(ram_1_data), .str(control_unit_1_memwrite),
    .sel(1'b1), .clk(not_1_out), .ld(control_unit_1_memread), .clr(in_2));
  Multiplexer #(.width(16), .enable("false")) multiplexer_6 (
    .in0(alu_1_aluresult), .in1(ram_1_data), .out(multiplexer_6_out), .sel(control_unit_1_memtoreg));

  // Notes on the sheet:
  //   contents of rom_1 (hex, n*v repeats v):
  //   3 25 4843 5268 2380 6c05 7426 9800 0 0 30 3
endmodule

module register_file (
  input  [2:0] Read_Register_1,
  input  Write,
  input  [2:0] Read_Register_2,
  input  [2:0] Write_Rigister,
  input  Clock,
  input  Reset,
  input  [15:0] Write_Data,
  output [15:0] Read_Data_1,
  output [15:0] Read_Data_2
);

  wire and_1_out, and_2_out, and_3_out, and_4_out, and_5_out, and_6_out, and_7_out, and_8_out,
       decoder_1_out0, decoder_1_out1, decoder_1_out2, decoder_1_out3, decoder_1_out4, decoder_1_out5,
       decoder_1_out6, decoder_1_out7;
  wire [15:0] r1_q, r2_q, r3_q, r4_q, r5_q, r6_q, r7_q, r8_q;

  Decoder #(.select(3)) decoder_1 (
    .out0(decoder_1_out0), .out1(decoder_1_out1), .out2(decoder_1_out2), .out3(decoder_1_out3),
    .out4(decoder_1_out4), .out5(decoder_1_out5), .out6(decoder_1_out6), .out7(decoder_1_out7),
    .sel(Write_Rigister), .en(1'b1));
  and and_1 (and_1_out, decoder_1_out0, Write);
  and and_2 (and_2_out, decoder_1_out1, Write);
  and and_3 (and_3_out, decoder_1_out2, Write);
  and and_4 (and_4_out, decoder_1_out3, Write);
  and and_5 (and_5_out, decoder_1_out4, Write);
  and and_6 (and_6_out, decoder_1_out5, Write);
  and and_7 (and_7_out, decoder_1_out6, Write);
  and and_8 (and_8_out, decoder_1_out7, Write);
  Register #(.width(16)) r1 (.D(Write_Data), .en(and_1_out), .Q(r1_q), .clk(Clock), .clr(Reset));
  Register #(.width(16)) r2 (.D(Write_Data), .en(and_2_out), .Q(r2_q), .clk(Clock), .clr(Reset));
  Register #(.width(16)) r3 (.D(Write_Data), .en(and_3_out), .Q(r3_q), .clk(Clock), .clr(Reset));
  Register #(.width(16)) r4 (.D(Write_Data), .en(and_4_out), .Q(r4_q), .clk(Clock), .clr(Reset));
  Register #(.width(16)) r5 (.D(Write_Data), .en(and_5_out), .Q(r5_q), .clk(Clock), .clr(Reset));
  Register #(.width(16)) r6 (.D(Write_Data), .en(and_6_out), .Q(r6_q), .clk(Clock), .clr(Reset));
  Register #(.width(16)) r7 (.D(Write_Data), .en(and_7_out), .Q(r7_q), .clk(Clock), .clr(Reset));
  Register #(.width(16)) r8 (.D(Write_Data), .en(and_8_out), .Q(r8_q), .clk(Clock), .clr(Reset));
  Multiplexer #(.select(3), .width(16)) multiplexer_1 (
    .in0(r1_q), .in1(r2_q), .in2(r3_q), .in3(r4_q), .in4(r5_q), .in5(r6_q), .in6(r7_q), .in7(r8_q),
    .out(Read_Data_1), .sel(Read_Register_1));  // open: en
  Multiplexer #(.select(3), .width(16)) multiplexer_2 (
    .in0(r1_q), .in1(r2_q), .in2(r3_q), .in3(r4_q), .in4(r5_q), .in5(r6_q), .in6(r7_q), .in7(r8_q),
    .out(Read_Data_2), .sel(Read_Register_2));  // open: en
endmodule

module Control_Unit (
  input  a,
  input  b,
  input  c,
  input  d,
  input  e,
  output RegDst,
  output RegWrite,
  output ALUSrc,
  output Branch,
  output MemRead,
  output MemWrite,
  output MemtoReg,
  output Li,
  output Write_ra,
  output Read_ra,
  output EnReboot,
  output Enjump
);

  wire and_1_out, and_2_out, and_3_out, and_4_out, and_5_out, and_6_out, and_7_out, and_8_out, and_9_out,
       and_10_out, and_11_out, and_12_out, and_13_out, and_14_out, and_15_out, and_16_out, and_17_out,
       and_18_out, and_19_out, and_20_out, and_21_out, and_22_out, and_23_out, and_24_out, and_25_out,
       and_26_out, and_27_out, and_28_out, and_30_out, and_31_out, and_32_out, not_1_out, not_2_out,
       not_3_out, not_4_out, not_5_out, not_6_out, not_7_out, not_8_out, not_9_out, not_10_out, not_11_out,
       not_12_out, not_13_out, not_14_out, not_15_out, not_16_out, not_17_out, not_18_out, not_19_out,
       not_20_out, not_21_out, not_22_out, not_23_out, not_24_out, not_25_out, not_26_out, not_27_out,
       not_28_out, not_29_out, not_30_out, not_31_out, not_32_out, not_33_out, not_34_out, not_35_out,
       not_36_out, not_37_out, not_38_out, not_39_out, not_40_out, not_41_out, not_42_out, not_43_out;

  not not_1 (not_1_out, a);
  not not_2 (not_2_out, b);
  not not_3 (not_3_out, c);
  not not_4 (not_4_out, a);
  not not_5 (not_5_out, b);
  not not_6 (not_6_out, c);
  not not_7 (not_7_out, d);
  not not_8 (not_8_out, e);
  not not_9 (not_9_out, a);
  not not_10 (not_10_out, b);
  not not_11 (not_11_out, a);
  not not_12 (not_12_out, c);
  not not_13 (not_13_out, d);
  not not_14 (not_14_out, a);
  not not_15 (not_15_out, d);
  not not_16 (not_16_out, a);
  not not_17 (not_17_out, e);
  not not_18 (not_18_out, a);
  not not_19 (not_19_out, c);
  not not_20 (not_20_out, d);
  not not_21 (not_21_out, e);
  not not_22 (not_22_out, c);
  not not_23 (not_23_out, d);
  not not_24 (not_24_out, c);
  not not_25 (not_25_out, e);
  not not_26 (not_26_out, c);
  not not_27 (not_27_out, e);
  not not_28 (not_28_out, c);
  not not_29 (not_29_out, b);
  not not_30 (not_30_out, d);
  not not_31 (not_31_out, b);
  not not_32 (not_32_out, e);
  not not_33 (not_33_out, b);
  not not_34 (not_34_out, d);
  not not_35 (not_35_out, a);
  not not_36 (not_36_out, d);
  not not_37 (not_37_out, e);
  not not_38 (not_38_out, d);
  not not_39 (not_39_out, e);
  not not_40 (not_40_out, d);
  not not_41 (not_41_out, e);
  not not_42 (not_42_out, d);
  not not_43 (not_43_out, e);
  and and_1 (and_1_out, not_1_out, not_2_out, not_3_out, e);
  and and_2 (and_2_out, not_4_out, not_5_out, not_6_out, d);
  and and_3 (and_3_out, b, c, not_7_out);
  and and_4 (and_4_out, b, c, not_8_out);
  and and_5 (and_5_out, a, b);
  and and_6 (and_6_out, not_9_out, not_10_out);
  and and_7 (and_7_out, not_11_out, not_12_out, not_13_out);
  and and_8 (and_8_out, not_14_out, not_15_out, e);
  and and_9 (and_9_out, not_16_out, d, not_17_out);
  and and_10 (and_10_out, a, b);
  and and_11 (and_11_out, not_18_out, not_19_out, not_20_out, not_21_out);
  and and_12 (and_12_out, b, not_22_out, not_23_out);
  and and_13 (and_13_out, b, not_24_out, not_25_out);
  and and_14 (and_14_out, a, not_26_out, d, not_27_out);
  and and_15 (and_15_out, a, b);
  and and_16 (and_16_out, b, not_28_out, d, e);
  and and_17 (and_17_out, a, b);
  and and_18 (and_18_out, not_29_out, c, not_30_out, e);
  and and_19 (and_19_out, a, b);
  and and_20 (and_20_out, not_31_out, c, d, not_32_out);
  and and_21 (and_21_out, a, c);
  and and_22 (and_22_out, a, b);
  and and_23 (and_23_out, not_33_out, c, not_34_out, e);
  and and_24 (and_24_out, a, b);
  or or_1 (Li, not_35_out, not_36_out, not_37_out, c);
  and and_25 (and_25_out, a, not_38_out, not_39_out);
  and and_26 (and_26_out, a, c);
  and and_27 (and_27_out, a, not_40_out, e);
  and and_28 (and_28_out, a, b);
  and and_29 (EnReboot, a, d, not_41_out);
  and and_30 (and_30_out, b, c, d, e);
  and and_31 (and_31_out, a, not_42_out, not_43_out);
  and and_32 (and_32_out, a, b);
  or or_2 (RegDst, and_1_out, and_2_out, and_3_out, and_4_out, and_5_out);
  or or_3 (RegWrite, and_6_out, and_7_out, and_8_out, and_9_out, and_10_out);
  or or_4 (ALUSrc, and_11_out, and_12_out, and_13_out, and_14_out, and_15_out);
  or or_5 (Branch, and_16_out, and_17_out);
  or or_6 (MemRead, and_18_out, and_19_out);
  or or_7 (MemWrite, and_20_out, and_21_out, and_22_out);
  or or_8 (MemtoReg, and_23_out, and_24_out);
  or or_9 (Write_ra, and_25_out, and_26_out);
  or or_10 (Read_ra, and_27_out, and_28_out);
  or or_11 (Enjump, and_30_out, and_31_out, and_32_out);
endmodule

module ALU (
  input  [15:0] ReadData1,
  input  [15:0] ReadData2,
  input  [3:0] ALUControl,
  output [15:0] ALUresult,
  output out_5
);

  wire comparator_1_eq, comparator_1_lt, or_2_out;
  wire [3:0] bit_extender_1_out, bit_extender_2_out;
  wire [15:0] adder_1_out, adder_2_out, adder_3_out, and_1_out, bit_extender_3_out, bit_extender_4_out,
       or_1_out, shifter_1_out, shifter_2_out, subtractor_1_out;

  Comparator #(.width(16)) comparator_1 (
    .a(ReadData1), .b(ReadData2), .eq(comparator_1_eq), .lt(comparator_1_lt));  // open: gt
  Bit_Extender #(.in_width(16), .out_width(4), .\type ("sign")) bit_extender_1 (
    .in(ReadData2), .out(bit_extender_1_out));
  Bit_Extender #(.in_width(16), .out_width(4), .\type ("sign")) bit_extender_2 (
    .in(ReadData2), .out(bit_extender_2_out));
  Adder #(.width(16)) adder_1 (.a({16{1'b0}}), .b(ReadData2), .out(adder_1_out));  // open: cin, cout
  Adder #(.width(16)) adder_2 (.a(ReadData1), .b(ReadData2), .out(adder_2_out));  // open: cin, cout
  assign and_1_out = ReadData1 & ReadData2;  // AND_Gate and_1, 16 bits wide
  assign or_1_out = ReadData1 | ReadData2;  // OR_Gate or_1, 16 bits wide
  Subtractor #(.width(16)) subtractor_1 (.a({16{1'b0}}), .b(ReadData1), .out(subtractor_1_out));  // open: bin, bout
  or or_2 (or_2_out, comparator_1_eq, comparator_1_lt);
  Shifter #(.width(16)) shifter_1 (.in(ReadData1), .\dist (bit_extender_1_out), .out(shifter_1_out));
  Shifter #(.width(16), .shift("lr")) shifter_2 (.in(ReadData1), .\dist (bit_extender_2_out), .out(shifter_2_out));
  Adder #(.width(16)) adder_3 (.a({16{1'b0}}), .b(ReadData1), .out(adder_3_out));  // open: cin, cout
  assign bit_extender_3_out = {{15{1'b0}}, or_2_out};  // Bit_Extender bit_extender_3
  assign bit_extender_4_out = {{15{1'b0}}, comparator_1_lt};  // Bit_Extender bit_extender_4
  Multiplexer #(.select(4), .width(16)) multiplexer_1 (
    .in0(adder_1_out), .in1(adder_2_out), .in2(and_1_out), .in3(or_1_out), .in4(subtractor_1_out),
    .in5(bit_extender_3_out), .in6(bit_extender_4_out), .in7(shifter_1_out), .in8(shifter_2_out),
    .in9(adder_3_out), .out(ALUresult), .sel(ALUControl), .en(1'b1));  // open: in10, in11, in12, in13, in14, in15
  Multiplexer #(.select(4)) multiplexer_2 (
    .in5(or_2_out), .in6(comparator_1_lt), .out(out_5), .sel(ALUControl), .en(1'b1));  // open: in0, in1, in2, in3, in4, in7, in8, in9, in10, in11, in12, in13, in14, in15
endmodule

module ALUControl (
  input  a,
  input  b,
  input  c,
  input  d,
  input  e,
  output x,
  output y,
  output z,
  output u
);

  wire and_1_out, and_2_out, and_3_out, and_4_out, and_5_out, and_6_out, and_7_out, and_8_out, and_9_out,
       and_10_out, and_11_out, and_12_out, and_13_out, and_14_out, and_15_out, not_1_out, not_2_out,
       not_3_out, not_4_out, not_5_out, not_6_out, not_7_out, not_8_out, not_9_out, not_10_out, not_11_out,
       not_12_out, not_13_out, not_14_out;

  not not_1 (not_1_out, b);
  not not_2 (not_2_out, d);
  not not_3 (not_3_out, e);
  not not_4 (not_4_out, d);
  not not_5 (not_5_out, b);
  not not_6 (not_6_out, c);
  not not_7 (not_7_out, c);
  not not_8 (not_8_out, e);
  not not_9 (not_9_out, d);
  not not_10 (not_10_out, d);
  not not_11 (not_11_out, b);
  not not_12 (not_12_out, b);
  not not_13 (not_13_out, c);
  not not_14 (not_14_out, e);
  and and_1 (and_1_out, not_1_out, c, e);
  and and_2 (and_2_out, c, d);
  and and_3 (and_3_out, c, not_2_out, not_3_out);
  and and_4 (and_4_out, b, d, e);
  and and_5 (and_5_out, b, c, not_4_out);
  and and_6 (and_6_out, not_5_out, not_6_out, d);
  and and_7 (and_7_out, not_7_out, d, not_8_out);
  and and_8 (and_8_out, b, not_9_out, e);
  and and_9 (and_9_out, b, c, not_10_out);
  and and_10 (and_10_out, b, c, e);
  and and_11 (and_11_out, not_11_out, e);
  and and_12 (and_12_out, d, e);
  and and_13 (and_13_out, c, e);
  and and_14 (and_14_out, not_12_out, c, d);
  and and_15 (and_15_out, b, not_13_out, not_14_out);
  or or_1 (x, and_1_out, and_2_out, a);
  or or_2 (y, and_3_out, and_4_out, and_5_out, a);
  or or_3 (z, and_6_out, and_7_out, and_8_out, and_9_out, and_10_out, a);
  or or_4 (u, and_11_out, and_12_out, and_13_out, and_14_out, and_15_out, a);
endmodule
