// Logisim project Pipelined_processor.circ as structural Verilog: 15 circuits, main circuit main
module main (
  input  RESET,
  output [2:0] out_2
);

  wire alu_1_jr, alu_1_zero, alu_control_1_lws, clock_1_out, control_unit_1_alusrc, control_unit_1_beq,
       control_unit_1_bneq, control_unit_1_extop, control_unit_1_jal, control_unit_1_jump,
       control_unit_1_lui, control_unit_1_memread, control_unit_1_memtoreg, control_unit_1_memwrite,
       control_unit_1_r_type, control_unit_1_regdest, control_unit_1_regwrite, execution_buffer_1_out_12,
       execution_buffer_1_out_13, execution_buffer_1_out_14, execution_buffer_1_out_15,
       instruction_decode_buffer_1_beq_output, instruction_decode_buffer_1_bneq_output,
       instruction_decode_buffer_1_extop_output, instruction_decode_buffer_1_jal_ouput,
       instruction_decode_buffer_1_jump_output, instruction_decode_buffer_1_memread_output,
       instruction_decode_buffer_1_memtoreg_output, instruction_decode_buffer_1_memwrite_output,
       instruction_decode_buffer_1_regdest_output, instruction_decode_buffer_1_regwrite_output,
       memory_buffer_1_out_10, memory_buffer_1_out_11, not_1_out, or_1_out, or_2_out;
  wire [1:0] forward_1_forwarda, forward_1_forwardb;
  wire [2:0] execution_buffer_1_out_9, instruction_decode_buffer_1_ra_output,
       instruction_decode_buffer_1_rb_output, memory_buffer_1_out_7, multiplexer_2_out, multiplexer_3_out,
       multiplexer_4_out, multiplexer_8_out, pc_control_1_pc;
  wire [3:0] alu_control_1_alu_control, control_unit_1_aluoperand,
       instruction_decode_buffer_1_alu_operand_function;
  wire [4:0] instruction_decode_buffer_1_imm_output;
  wire [15:0] adder_1_out, adder_2_out, adder_3_out, alu_1_ouput_data, bit_extender_1_out,
       execution_buffer_1_alu_result_output, execution_buffer_1_out_11, extender_1_output,
       instruction_decode_buffer_1_bus_a_output, instruction_decode_buffer_1_bus_b_output,
       instruction_decode_buffer_1_j_type_imm_out, instruction_decode_buffer_1_pc_output,
       instruction_fetch_buffer_1_ir_output, instruction_fetch_buffer_1_pc_output, JR,
       memory_buffer_1_aluresult_output, memory_buffer_1_memresult_output, multiplexer_1_out,
       multiplexer_5_out, multiplexer_6_out, multiplexer_7_out, multiplexer_9_out, multiplexer_10_out,
       multiplexer_11_out, multiplexer_12_out, PC_q, ram_1_data, ram_2_data, registers_1_bus_a,
       registers_1_bus_b;

  Multiplexer #(.select(3), .width(16), .enable("false")) multiplexer_1 (
    .in0(adder_1_out), .in1(instruction_decode_buffer_1_j_type_imm_out), .in2(adder_3_out), .in3(JR),
    .in4(adder_3_out), .out(multiplexer_1_out), .sel(pc_control_1_pc));  // open: in5, in6, in7
  Register #(.width(16)) PC (.D(multiplexer_1_out), .Q(PC_q), .clk(clock_1_out));  // open: en, clr
  Clock clock_1 (.out(clock_1_out));
  Adder #(.width(16)) adder_1 (.a(PC_q), .b(16'h1), .out(adder_1_out));  // open: cin, cout
  RAM #(.addrWidth(16), .dataWidth(16)) ram_1 (
    .addr(PC_q), .data(ram_1_data), .sel(1'b1), .ld(1'b1));  // open: clk, clr
  instruction_fetch_buffer instruction_fetch_buffer_1 (
    .PC(adder_1_out), .IR(ram_1_data), .PC_Output(instruction_fetch_buffer_1_pc_output),
    .IR_Output(instruction_fetch_buffer_1_ir_output), .CLK(clock_1_out));
  assign bit_extender_1_out = {{5{instruction_fetch_buffer_1_ir_output[10]}}, instruction_fetch_buffer_1_ir_output[10:0]};  // Bit_Extender bit_extender_1
  control_unit control_unit_1 (
    .Jal(control_unit_1_jal), .Jump(control_unit_1_jump), .RegDest(control_unit_1_regdest),
    .BEQ(control_unit_1_beq), .MemWrite(control_unit_1_memwrite), .MemRead(control_unit_1_memread),
    .MemToReg(control_unit_1_memtoreg), .RegWrite(control_unit_1_regwrite), .BNEQ(control_unit_1_bneq),
    .ALUSrc(control_unit_1_alusrc), .ExtOp(control_unit_1_extop), .AluOperand(control_unit_1_aluoperand),
    .Opcode(instruction_fetch_buffer_1_ir_output[15:11]), .R_Type(control_unit_1_r_type),
    .LUI(control_unit_1_lui));
  Multiplexer #(.width(3), .enable("false")) multiplexer_2 (
    .in0(instruction_fetch_buffer_1_ir_output[2:0]), .in1(memory_buffer_1_out_7), .out(multiplexer_2_out),
    .sel(control_unit_1_regdest));
  Adder #(.width(16)) adder_2 (
    .a(bit_extender_1_out), .b(instruction_fetch_buffer_1_pc_output), .out(adder_2_out));  // open: cin, cout
  Multiplexer #(.width(3), .enable("false")) multiplexer_3 (
    .in0(multiplexer_2_out), .in1(3'b111), .out(multiplexer_3_out),
    .sel(instruction_decode_buffer_1_jal_ouput));
  or or_1 (or_1_out, control_unit_1_memtoreg, control_unit_1_memread, alu_control_1_lws);
  Multiplexer #(.width(3), .enable("false")) multiplexer_4 (
    .in0(instruction_fetch_buffer_1_ir_output[2:0]), .in1(3'b001), .out(multiplexer_4_out),
    .sel(control_unit_1_lui));
  registers registers_1 (
    .BUS_W(multiplexer_5_out), .Clock(clock_1_out), .RegWrite(memory_buffer_1_out_11),
    .RB(instruction_fetch_buffer_1_ir_output[2:0]), .RA(instruction_fetch_buffer_1_ir_output[5:3]),
    .Clear_Flag(RESET), .RW(multiplexer_3_out), .BUS_A(registers_1_bus_a), .BUS_B(registers_1_bus_b));
  alu_control alu_control_1 (
    .Opcode(instruction_fetch_buffer_1_ir_output[15:11]), .Main_Control(control_unit_1_aluoperand),
    .Function(instruction_fetch_buffer_1_ir_output[10:9]), .ALU_Control(alu_control_1_alu_control),
    .LWS(alu_control_1_lws), .Type(control_unit_1_r_type));
  Multiplexer #(.width(16), .enable("false")) multiplexer_5 (
    .in0(multiplexer_12_out), .in1(instruction_decode_buffer_1_pc_output), .out(multiplexer_5_out),
    .sel(instruction_decode_buffer_1_jal_ouput));
  Multiplexer #(.width(16), .enable("false")) multiplexer_6 (
    .in0(registers_1_bus_a), .in1(bit_extender_1_out), .out(multiplexer_6_out), .sel(control_unit_1_lui));
  Multiplexer #(.width(16), .enable("false")) multiplexer_7 (
    .in0(registers_1_bus_b), .in1(16'h5), .out(multiplexer_7_out), .sel(control_unit_1_lui));
  Adder #(.width(16)) adder_3 (
    .a(instruction_decode_buffer_1_pc_output), .b(extender_1_output), .out(adder_3_out));  // open: cin, cout
  instruction_decode_buffer instruction_decode_buffer_1 (
    .J_Type_Imm_In(adder_2_out), .RB_In(multiplexer_4_out),
    .RD_In(instruction_fetch_buffer_1_ir_output[8:6]), .PC_In(instruction_fetch_buffer_1_pc_output),
    .Imm_In(instruction_fetch_buffer_1_ir_output[10:6]), .Bus_A_In(multiplexer_6_out),
    .Bus_B_In(multiplexer_7_out), .Alu_Operand(alu_control_1_alu_control), .JAL_In(control_unit_1_jal),
    .Jump_In(control_unit_1_jump), .RegDest_In(control_unit_1_regdest), .BEQ_In(control_unit_1_beq),
    .MemWrite_In(control_unit_1_memwrite), .MemRead_In(or_1_out), .MemToReg_In(control_unit_1_memtoreg),
    .RegWrite_In(control_unit_1_regwrite), .BNEQ_In(control_unit_1_bneq), .AluSrc_In(control_unit_1_alusrc),
    .ExtOp_In(control_unit_1_extop), .J_Type_Imm_Out(instruction_decode_buffer_1_j_type_imm_out),
    .RA_Output(instruction_decode_buffer_1_ra_output), .RB_Output(instruction_decode_buffer_1_rb_output),
    .RD_Output(out_2), .PC_Output(instruction_decode_buffer_1_pc_output),
    .Imm_Output(instruction_decode_buffer_1_imm_output),
    .Bus_A_Output(instruction_decode_buffer_1_bus_a_output),
    .Bus_B_Output(instruction_decode_buffer_1_bus_b_output),
    .Alu_Operand_Function(instruction_decode_buffer_1_alu_operand_function),
    .JAL_Ouput(instruction_decode_buffer_1_jal_ouput), .Jump_Output(instruction_decode_buffer_1_jump_output),
    .RegDest_Output(instruction_decode_buffer_1_regdest_output),
    .BEQ_Output(instruction_decode_buffer_1_beq_output),
    .MemWrite_Output(instruction_decode_buffer_1_memwrite_output),
    .MemRead_Output(instruction_decode_buffer_1_memread_output),
    .MemToReg_Output(instruction_decode_buffer_1_memtoreg_output),
    .RegWrite_Output(instruction_decode_buffer_1_regwrite_output),
    .BNEQ_Output(instruction_decode_buffer_1_bneq_output),
    .ExtOp_Output(instruction_decode_buffer_1_extop_output), .CLK(clock_1_out),
    .RA_In(instruction_fetch_buffer_1_ir_output[5:3]));  // open: AluSrc_Output
  extender extender_1 (
    .ExtOp(instruction_decode_buffer_1_extop_output), .Imm(instruction_decode_buffer_1_imm_output),
    .Output(extender_1_output));
  Multiplexer #(.width(3), .enable("false")) multiplexer_8 (
    .in0(instruction_decode_buffer_1_rb_output), .in1(out_2), .out(multiplexer_8_out),
    .sel(instruction_decode_buffer_1_regdest_output));
  Multiplexer #(.select(2), .width(16), .enable("false")) multiplexer_9 (
    .in0(instruction_decode_buffer_1_bus_a_output), .in1(multiplexer_12_out),
    .in2(execution_buffer_1_alu_result_output), .out(multiplexer_9_out), .sel(forward_1_forwarda));  // open: in3
  Multiplexer #(.select(2), .width(16), .enable("false")) multiplexer_10 (
    .in0(instruction_decode_buffer_1_bus_b_output), .in1(multiplexer_12_out),
    .in2(execution_buffer_1_alu_result_output), .out(multiplexer_10_out), .sel(forward_1_forwardb));  // open: in3
  pc_control pc_control_1 (
    .PC(pc_control_1_pc), .JR(alu_1_jr), .JUMP(instruction_decode_buffer_1_jump_output), .ZERO(alu_1_zero),
    .BEQ(instruction_decode_buffer_1_beq_output), .BNEQ(instruction_decode_buffer_1_bneq_output),
    .rs(instruction_decode_buffer_1_ra_output));
  Multiplexer #(.width(16), .enable("false")) multiplexer_11 (
    .in0(extender_1_output), .in1(multiplexer_10_out), .out(multiplexer_11_out), .sel(not_1_out));
  not not_1 (not_1_out, instruction_decode_buffer_1_extop_output);
  forward forward_1 (
    .RT(instruction_decode_buffer_1_rb_output), .Rd_mem(execution_buffer_1_out_9),
    .Rd_wb(memory_buffer_1_out_7), .RegisterWrite_Men(execution_buffer_1_out_15),
    .RegisterWrite_WB(memory_buffer_1_out_11), .ForwardA(forward_1_forwarda), .ForwardB(forward_1_forwardb),
    .RS(instruction_decode_buffer_1_ra_output));
  alu alu_1 (
    .Bus_A(multiplexer_9_out), .Bus_B(multiplexer_11_out),
    .AluControl(instruction_decode_buffer_1_alu_operand_function), .Zero(alu_1_zero), .JR(alu_1_jr),
    .Ouput_Data(alu_1_ouput_data));
  execution_buffer execution_buffer_1 (
    .in_1(multiplexer_8_out), .Alu_Result_In(alu_1_ouput_data), .in_3(multiplexer_10_out),
    .MemWrite_In(instruction_decode_buffer_1_memwrite_output),
    .MemRead_In(instruction_decode_buffer_1_memread_output),
    .MemToReg_In(instruction_decode_buffer_1_memtoreg_output),
    .RegWrite_In(instruction_decode_buffer_1_regwrite_output), .out_9(execution_buffer_1_out_9),
    .Alu_Result_Output(execution_buffer_1_alu_result_output), .out_11(execution_buffer_1_out_11),
    .out_12(execution_buffer_1_out_12), .out_13(execution_buffer_1_out_13),
    .out_14(execution_buffer_1_out_14), .out_15(execution_buffer_1_out_15), .CLK(clock_1_out));
  or or_2 (or_2_out, execution_buffer_1_out_12, execution_buffer_1_out_13);
  RAM #(.addrWidth(16), .dataWidth(16), .bus("separate")) ram_2 (
    .addr(execution_buffer_1_alu_result_output), .din(execution_buffer_1_out_11), .data(ram_2_data),
    .str(execution_buffer_1_out_12), .sel(or_2_out), .clk(clock_1_out), .ld(execution_buffer_1_out_13),
    .clr(1'b0));
  memory_buffer memory_buffer_1 (
    .in_1(execution_buffer_1_out_9), .AluResult_In(execution_buffer_1_alu_result_output),
    .MemResult_In(ram_2_data), .MemToReg_In(execution_buffer_1_out_14),
    .RegWrite_In(execution_buffer_1_out_15), .out_7(memory_buffer_1_out_7),
    .AluResult_Output(memory_buffer_1_aluresult_output), .MemResult_Output(memory_buffer_1_memresult_output),
    .out_10(memory_buffer_1_out_10), .out_11(memory_buffer_1_out_11), .CLK(clock_1_out));
  Multiplexer #(.width(16), .enable("false")) multiplexer_12 (
    .in0(memory_buffer_1_aluresult_output), .in1(memory_buffer_1_memresult_output), .out(multiplexer_12_out),
    .sel(memory_buffer_1_out_10));

  // Notes on the sheet:
  //   INSTRUCTION MEMORY
endmodule

// Register
module register (
  input  Clock,
  input  [15:0] Input,
  input  Write_Flag,
  input  Clear_Flag,
  output [15:0] Output
);

  wire Clear_Flag_t, d_ff_1_q, d_ff_2_q, d_ff_3_q, d_ff_4_q, d_ff_5_q, d_ff_6_q, d_ff_7_q, d_ff_8_q,
       d_ff_9_q, d_ff_10_q, d_ff_11_q, d_ff_12_q, d_ff_13_q, d_ff_14_q, d_ff_15_q, d_ff_16_q;

  not not_1 (Clear_Flag_t, Clear_Flag);
  D_Flip_Flop d_ff_1 (.clk(Clock), .D(Input[15]), .Q(d_ff_1_q), .en(Write_Flag));  // open: Qn, preset, reset
  and and_1 (Output[15], Clear_Flag_t, d_ff_1_q);
  D_Flip_Flop d_ff_2 (.clk(Clock), .D(Input[14]), .Q(d_ff_2_q), .en(Write_Flag));  // open: Qn, preset, reset
  and and_2 (Output[14], Clear_Flag_t, d_ff_2_q);
  D_Flip_Flop d_ff_3 (.clk(Clock), .D(Input[13]), .Q(d_ff_3_q), .en(Write_Flag));  // open: Qn, preset, reset
  and and_3 (Output[13], Clear_Flag_t, d_ff_3_q);
  D_Flip_Flop d_ff_4 (.clk(Clock), .D(Input[12]), .Q(d_ff_4_q), .en(Write_Flag));  // open: Qn, preset, reset
  and and_4 (Output[12], Clear_Flag_t, d_ff_4_q);
  D_Flip_Flop d_ff_5 (.clk(Clock), .D(Input[11]), .Q(d_ff_5_q), .en(Write_Flag));  // open: Qn, preset, reset
  and and_5 (Output[11], Clear_Flag_t, d_ff_5_q);
  D_Flip_Flop d_ff_6 (.clk(Clock), .D(Input[10]), .Q(d_ff_6_q), .en(Write_Flag));  // open: Qn, preset, reset
  and and_6 (Output[10], Clear_Flag_t, d_ff_6_q);
  D_Flip_Flop d_ff_7 (.clk(Clock), .D(Input[9]), .Q(d_ff_7_q), .en(Write_Flag));  // open: Qn, preset, reset
  and and_7 (Output[9], Clear_Flag_t, d_ff_7_q);
  and and_8 (Output[8], Clear_Flag_t, d_ff_8_q);
  D_Flip_Flop d_ff_8 (.clk(Clock), .D(Input[8]), .Q(d_ff_8_q), .en(Write_Flag));  // open: Qn, preset, reset
  D_Flip_Flop d_ff_9 (.clk(Clock), .D(Input[7]), .Q(d_ff_9_q), .en(Write_Flag));  // open: Qn, preset, reset
  and and_9 (Output[7], Clear_Flag_t, d_ff_9_q);
  D_Flip_Flop d_ff_10 (.clk(Clock), .D(Input[6]), .Q(d_ff_10_q), .en(Write_Flag));  // open: Qn, preset, reset
  and and_10 (Output[6], Clear_Flag_t, d_ff_10_q);
  D_Flip_Flop d_ff_11 (.clk(Clock), .D(Input[5]), .Q(d_ff_11_q), .en(Write_Flag));  // open: Qn, preset, reset
  and and_11 (Output[5], Clear_Flag_t, d_ff_11_q);
  D_Flip_Flop d_ff_12 (.clk(Clock), .D(Input[4]), .Q(d_ff_12_q), .en(Write_Flag));  // open: Qn, preset, reset
  and and_12 (Output[4], Clear_Flag_t, d_ff_12_q);
  D_Flip_Flop d_ff_13 (.clk(Clock), .D(Input[3]), .Q(d_ff_13_q), .en(Write_Flag));  // open: Qn, preset, reset
  and and_13 (Output[3], Clear_Flag_t, d_ff_13_q);
  D_Flip_Flop d_ff_14 (.clk(Clock), .D(Input[2]), .Q(d_ff_14_q), .en(Write_Flag));  // open: Qn, preset, reset
  and and_14 (Output[2], Clear_Flag_t, d_ff_14_q);
  D_Flip_Flop d_ff_15 (.clk(Clock), .D(Input[1]), .Q(d_ff_15_q), .en(Write_Flag));  // open: Qn, preset, reset
  and and_15 (Output[1], Clear_Flag_t, d_ff_15_q);
  and and_16 (Output[0], Clear_Flag_t, d_ff_16_q);
  D_Flip_Flop d_ff_16 (.clk(Clock), .D(Input[0]), .Q(d_ff_16_q), .en(Write_Flag));  // open: Qn, preset, reset
endmodule

module registers (
  input  [15:0] BUS_W,
  input  Clock,
  input  RegWrite,
  input  [2:0] RW,
  input  Clear_Flag,
  input  [2:0] RA,
  input  [2:0] RB,
  output [15:0] BUS_A,
  output [15:0] BUS_B
);

  wire R1, R2, R3, R4, R5, R6, R7;
  wire [15:0] Register_1_output, Register_2_output, Register_3_output, Register_4_output, Register_5_output,
       Register_6_output, Register_7_output;

  register Register_1 (
    .Clock(Clock), .Write_Flag(R1), .Input(BUS_W), .Output(Register_1_output), .Clear_Flag(Clear_Flag));
  Decoder #(.select(3)) decoder_1 (
    .out1(R1), .out2(R2), .out3(R3), .out4(R4), .out5(R5), .out6(R6), .out7(R7), .sel(RW), .en(RegWrite));  // open: out0
  register Register_2 (
    .Clock(Clock), .Write_Flag(R2), .Input(BUS_W), .Output(Register_2_output), .Clear_Flag(Clear_Flag));
  register Register_3 (
    .Clock(Clock), .Write_Flag(R3), .Input(BUS_W), .Output(Register_3_output), .Clear_Flag(Clear_Flag));
  Multiplexer #(.select(3), .width(16), .enable("false")) multiplexer_1 (
    .in0({16{1'b0}}), .in1(Register_1_output), .in2(Register_2_output), .in3(Register_3_output),
    .in4(Register_4_output), .in5(Register_5_output), .in6(Register_6_output), .in7(Register_7_output),
    .out(BUS_A), .sel(RA));
  register Register_4 (
    .Clock(Clock), .Write_Flag(R4), .Input(BUS_W), .Output(Register_4_output), .Clear_Flag(Clear_Flag));
  register Register_5 (
    .Clock(Clock), .Write_Flag(R5), .Input(BUS_W), .Output(Register_5_output), .Clear_Flag(Clear_Flag));
  Multiplexer #(.select(3), .width(16), .enable("false")) multiplexer_2 (
    .in0({16{1'b0}}), .in1(Register_1_output), .in2(Register_2_output), .in3(Register_3_output),
    .in4(Register_4_output), .in5(Register_5_output), .in6(Register_6_output), .in7(Register_7_output),
    .out(BUS_B), .sel(RB));
  register Register_6 (
    .Clock(Clock), .Write_Flag(R6), .Input(BUS_W), .Output(Register_6_output), .Clear_Flag(Clear_Flag));
  register Register_7 (
    .Clock(Clock), .Write_Flag(R7), .Input(BUS_W), .Output(Register_7_output), .Clear_Flag(Clear_Flag));

  // Other names for the same wires on the sheet: DB[15:0] = BUS_W

  // Notes on the sheet:
  //   Register 0
endmodule

module extender (
  input  [4:0] Imm,
  input  ExtOp,
  output [15:0] Output
);

  wire [15:0] bit_extender_1_out, bit_extender_2_out;

  assign bit_extender_1_out = {{11{1'b0}}, Imm};  // Bit_Extender bit_extender_1
  Multiplexer #(.width(16)) multiplexer_1 (
    .in0(bit_extender_1_out), .in1(bit_extender_2_out), .out(Output), .sel(ExtOp));  // open: en
  assign bit_extender_2_out = {{11{Imm[4]}}, Imm};  // Bit_Extender bit_extender_2
endmodule

module control_unit (
  input  [4:0] Opcode,
  output Jal,
  output Jump,
  output RegDest,
  output BEQ,
  output MemWrite,
  output MemRead,
  output MemToReg,
  output RegWrite,
  output BNEQ,
  output ALUSrc,
  output R_Type,
  output ExtOp,
  output LUI,
  output [3:0] AluOperand
);

  wire ADDI_out, ANDI_out, J_out, or_2_out, or_3_out, or_4_out, ORI_out, R_type_2_out, R_type_3_out,
       R_type_out, ROR_out, SLL_out, SRA_out, SRL_out, XORI_out;

  and u_R_type (R_type_out, ~Opcode[4], ~Opcode[3], ~Opcode[2], Opcode[1], ~Opcode[0]);  // AND_Gate
  and R_type_2 (R_type_2_out, ~Opcode[4], ~Opcode[3], ~Opcode[2], ~Opcode[1], Opcode[0]);  // AND_Gate
  or or_1 (R_Type, R_type_out, R_type_2_out, R_type_3_out);
  and R_type_3 (R_type_3_out, ~Opcode[4], ~Opcode[3], ~Opcode[2], ~Opcode[1], ~Opcode[0]);  // AND_Gate
  and LW (MemRead, ~Opcode[4], Opcode[3], Opcode[2], ~Opcode[1], ~Opcode[0]);  // AND_Gate
  and SW (MemWrite, ~Opcode[4], Opcode[3], Opcode[2], ~Opcode[1], Opcode[0]);  // AND_Gate
  or or_2 (or_2_out, MemRead, MemWrite, ADDI_out);
  and u_BEQ (BEQ, ~Opcode[4], Opcode[3], Opcode[2], Opcode[1], ~Opcode[0]);  // AND_Gate
  or or_3 (or_3_out, BEQ, BNEQ);
  and ADDI (ADDI_out, ~Opcode[4], ~Opcode[3], Opcode[2], Opcode[1], Opcode[0]);  // AND_Gate
  and SLL (SLL_out, ~Opcode[4], Opcode[3], ~Opcode[2], ~Opcode[1], ~Opcode[0]);  // AND_Gate
  or or_4 (or_4_out, SLL_out, LUI);
  and ANDI (ANDI_out, ~Opcode[4], ~Opcode[3], Opcode[2], ~Opcode[1], ~Opcode[0]);  // AND_Gate
  and ORI (ORI_out, ~Opcode[4], ~Opcode[3], Opcode[2], ~Opcode[1], Opcode[0]);  // AND_Gate
  and XORI (XORI_out, ~Opcode[4], ~Opcode[3], Opcode[2], Opcode[1], ~Opcode[0]);  // AND_Gate
  and SRL (SRL_out, ~Opcode[4], Opcode[3], ~Opcode[2], ~Opcode[1], Opcode[0]);  // AND_Gate
  and SRA (SRA_out, ~Opcode[4], Opcode[3], ~Opcode[2], Opcode[1], ~Opcode[0]);  // AND_Gate
  and ROR (ROR_out, ~Opcode[4], Opcode[3], ~Opcode[2], Opcode[1], Opcode[0]);  // AND_Gate
  Priority_Encoder #(.select(4)) priority_encoder_1 (
    .in0(ANDI_out), .in1(ORI_out), .in2(XORI_out), .in4(or_2_out), .in5(or_3_out), .in8(or_4_out),
    .in9(SRL_out), .in10(SRA_out), .in11(ROR_out), .out(AluOperand));  // open: in3, in6, in7, in12, in13, in14, in15, gs, en_out, en_in
  and BNE (BNEQ, ~Opcode[4], Opcode[3], Opcode[2], Opcode[1], Opcode[0]);  // AND_Gate
  and J (J_out, Opcode[4], Opcode[3], Opcode[2], Opcode[1], ~Opcode[0]);  // AND_Gate
  and u_LUI (LUI, Opcode[4], ~Opcode[3], ~Opcode[2], ~Opcode[1], ~Opcode[0]);  // AND_Gate
  and u_JAL (Jal, Opcode[4], Opcode[3], Opcode[2], Opcode[1], Opcode[0]);
  or or_5 (Jump, Jal, J_out);
  or or_6 (RegWrite, Jal, XORI_out, MemRead, LUI, ANDI_out, ADDI_out, R_Type, ORI_out);
  or or_7 (ALUSrc, XORI_out, ORI_out, MemRead, R_Type, MemWrite, ADDI_out, ANDI_out);
  or or_8 (ExtOp, MemWrite, ADDI_out, SLL_out, ANDI_out, ORI_out, XORI_out, SRL_out, SRA_out, ROR_out);

  assign MemToReg = MemRead;
  assign RegDest = R_Type;
endmodule

module alu_control (
  input  [4:0] Opcode,
  input  [3:0] Main_Control,
  input  [1:0] Function,
  input  Type,
  output [3:0] ALU_Control,
  output LWS
);

  wire [3:0] rtype_controller_1_alu_operand;

  rtype_controller rtype_controller_1 (
    .Function(Function), .Alu_Operand(rtype_controller_1_alu_operand), .Opcode(Opcode));
  Multiplexer #(.width(4), .enable("false")) multiplexer_1 (
    .in0(Main_Control), .in1(rtype_controller_1_alu_operand), .out(ALU_Control), .sel(Type));
  and and_1 (LWS, ~ALU_Control[0], ~ALU_Control[1], ALU_Control[2], ~ALU_Control[3]);  // AND_Gate
endmodule

module rtype_controller (
  input  [4:0] Opcode,
  input  [1:0] Function,
  output [3:0] Alu_Operand
);

  wire ADD_out, AND_out, JR_out, NOR_out, OR_out, R_type_2_out, R_type_3_out, R_type_out, SLT_out, SLTU_out,
       SUB_out, XOR_out;

  and R_type (R_type_out, ~Opcode[4], ~Opcode[3], ~Opcode[2], Opcode[1], ~Opcode[0]);  // AND_Gate
  and JR (JR_out, ~Function[1], ~Function[0], R_type_out);  // AND_Gate
  and R_type_2 (R_type_2_out, ~Opcode[4], ~Opcode[3], ~Opcode[2], ~Opcode[1], Opcode[0]);  // AND_Gate
  and ADD (ADD_out, ~Function[1], ~Function[0], R_type_2_out);  // AND_Gate
  and SUB (SUB_out, ~Function[1], Function[0], R_type_2_out);  // AND_Gate
  and SLT (SLT_out, Function[1], ~Function[0], R_type_2_out);  // AND_Gate
  and SLTU (SLTU_out, Function[1], Function[0], R_type_2_out);
  and R_type_3 (R_type_3_out, ~Opcode[4], ~Opcode[3], ~Opcode[2], ~Opcode[1], ~Opcode[0]);  // AND_Gate
  and AND (AND_out, ~Function[1], ~Function[0], R_type_3_out);  // AND_Gate
  and OR (OR_out, ~Function[1], Function[0], R_type_3_out);  // AND_Gate
  and XOR (XOR_out, Function[1], ~Function[0], R_type_3_out);  // AND_Gate
  and NOR (NOR_out, Function[1], Function[0], R_type_3_out);
  Priority_Encoder #(.select(4)) priority_encoder_1 (
    .in0(AND_out), .in1(OR_out), .in2(XOR_out), .in3(NOR_out), .in4(ADD_out), .in5(SUB_out), .in6(SLT_out),
    .in7(JR_out), .in12(SLTU_out), .out(Alu_Operand));  // open: in8, in9, in10, in11, in13, in14, in15, gs, en_out, en_in
endmodule

module alu (
  input  [15:0] Bus_A,
  input  [15:0] Bus_B,
  input  [3:0] AluControl,
  output [15:0] Ouput_Data,
  output Zero,
  output JR
);

  wire comparator_1_lt, comparator_2_lt;
  wire [3:0] bitselector_1_out;
  wire [15:0] adder_1_out, AND_out, bit_extender_1_out, bit_extender_2_out, NOR_out, OR_out, shifter_1_out,
       shifter_2_out, shifter_3_out, shifter_4_out, subtractor_1_out, XOR_out;

  assign AND_out = Bus_B & Bus_A;  // AND_Gate AND, 16 bits wide
  assign OR_out = Bus_B | Bus_A;  // OR_Gate OR, 16 bits wide
  assign XOR_out = Bus_B ^ Bus_A;  // XOR_Gate XOR, 16 bits wide
  assign NOR_out = ~(Bus_B | Bus_A);  // NOR_Gate NOR, 16 bits wide
  and and_2 (JR, ~AluControl[0], AluControl[1], AluControl[2], AluControl[3]);  // AND_Gate
  Adder #(.width(16)) adder_1 (.a(Bus_A), .b(Bus_B), .out(adder_1_out));  // open: cin, cout
  Subtractor #(.width(16)) subtractor_1 (.a(Bus_A), .b(Bus_B), .out(subtractor_1_out));  // open: bin, bout
  Multiplexer #(.select(4), .width(16), .enable("false")) multiplexer_1 (
    .in0(AND_out), .in1(OR_out), .in2(XOR_out), .in3(NOR_out), .in4(adder_1_out), .in5(subtractor_1_out),
    .in6(bit_extender_1_out), .in7(Bus_A), .in8(shifter_1_out), .in9(shifter_2_out), .in10(shifter_3_out),
    .in11(shifter_4_out), .in12(bit_extender_2_out), .out(Ouput_Data), .sel(AluControl));  // open: in13, in14, in15
  assign bit_extender_1_out = {{15{1'b0}}, comparator_1_lt};  // Bit_Extender bit_extender_1
  Comparator #(.width(16)) comparator_1 (.a(Bus_A), .b(Bus_B), .lt(comparator_1_lt));  // open: gt, eq
  assign bit_extender_2_out = {{15{1'b0}}, comparator_2_lt};  // Bit_Extender bit_extender_2
  Comparator #(.width(16), .mode("unsigned")) comparator_2 (
    .a(Bus_A), .b(Bus_B), .lt(comparator_2_lt));  // open: gt, eq
  BitSelector #(.width(16), .group(4)) bitselector_1 (.in(Bus_B), .out(bitselector_1_out), .sel(2'b00));
  Shifter #(.width(16)) shifter_1 (.in(Bus_A), .\dist (bitselector_1_out), .out(shifter_1_out));
  nor nor_2 (Zero, Ouput_Data[0], Ouput_Data[1], Ouput_Data[2], Ouput_Data[3], Ouput_Data[4], Ouput_Data[5], Ouput_Data[6], Ouput_Data[7], Ouput_Data[8], Ouput_Data[9], Ouput_Data[10], Ouput_Data[11], Ouput_Data[12], Ouput_Data[13], Ouput_Data[14], Ouput_Data[15]);
  Shifter #(.width(16), .shift("lr")) shifter_2 (.in(Bus_A), .\dist (bitselector_1_out), .out(shifter_2_out));
  Shifter #(.width(16), .shift("ar")) shifter_3 (.in(Bus_A), .\dist (bitselector_1_out), .out(shifter_3_out));
  Shifter #(.width(16), .shift("rr")) shifter_4 (.in(Bus_A), .\dist (bitselector_1_out), .out(shifter_4_out));

  // Notes on the sheet:
  //   ADD
  //   SUB
  //   SLT
  //   SLTU
  //   SLL
  //   SRL
  //   SRA
  //   ROR
endmodule

module instruction_fetch_buffer (
  input  CLK,
  input  [15:0] PC,
  input  [15:0] IR,
  output [15:0] PC_Output,
  output [15:0] IR_Output
);

  Register #(.width(16)) register_1 (.D(PC), .Q(PC_Output), .clk(CLK));  // open: en, clr
  Register #(.width(16)) register_2 (.D(IR), .Q(IR_Output), .clk(CLK));  // open: en, clr
endmodule

module instruction_decode_buffer (
  input  [15:0] J_Type_Imm_In,
  input  [2:0] RA_In,
  input  [2:0] RB_In,
  input  [2:0] RD_In,
  input  [15:0] PC_In,
  input  [4:0] Imm_In,
  input  [15:0] Bus_A_In,
  input  [15:0] Bus_B_In,
  input  [3:0] Alu_Operand,
  input  JAL_In,
  input  Jump_In,
  input  RegDest_In,
  input  BEQ_In,
  input  MemWrite_In,
  input  MemRead_In,
  input  MemToReg_In,
  input  RegWrite_In,
  input  BNEQ_In,
  input  AluSrc_In,
  input  ExtOp_In,
  input  CLK,
  output [15:0] J_Type_Imm_Out,
  output [2:0] RA_Output,
  output [2:0] RB_Output,
  output [2:0] RD_Output,
  output [15:0] PC_Output,
  output [4:0] Imm_Output,
  output [15:0] Bus_A_Output,
  output [15:0] Bus_B_Output,
  output [3:0] Alu_Operand_Function,
  output JAL_Ouput,
  output Jump_Output,
  output RegDest_Output,
  output BEQ_Output,
  output MemWrite_Output,
  output MemRead_Output,
  output MemToReg_Output,
  output RegWrite_Output,
  output BNEQ_Output,
  output AluSrc_Output,
  output ExtOp_Output
);

  Register #(.width(16)) register_1 (.D(J_Type_Imm_In), .Q(J_Type_Imm_Out), .clk(CLK));  // open: en, clr
  Register #(.width(3)) register_2 (.D(RA_In), .Q(RA_Output), .clk(CLK));  // open: en, clr
  Register #(.width(3)) register_3 (.D(RB_In), .Q(RB_Output), .clk(CLK));  // open: en, clr
  Register #(.width(3)) register_4 (.D(RD_In), .Q(RD_Output), .clk(CLK));  // open: en, clr
  Register #(.width(16)) register_5 (.D(PC_In), .Q(PC_Output), .clk(CLK));  // open: en, clr
  Register #(.width(5)) register_6 (.D(Imm_In), .Q(Imm_Output), .clk(CLK));  // open: en, clr
  Register #(.width(16)) register_7 (.D(Bus_A_In), .Q(Bus_A_Output), .clk(CLK));  // open: en, clr
  Register #(.width(16)) register_8 (.D(Bus_B_In), .Q(Bus_B_Output), .clk(CLK));  // open: en, clr
  Register #(.width(4)) register_9 (.D(Alu_Operand), .Q(Alu_Operand_Function), .clk(CLK));  // open: en, clr
  Register #(.width(1)) register_10 (.D(JAL_In), .Q(JAL_Ouput), .clk(CLK));  // open: en, clr
  Register #(.width(1)) register_11 (.D(Jump_In), .Q(Jump_Output), .clk(CLK));  // open: en, clr
  Register #(.width(1)) register_12 (.D(RegDest_In), .Q(RegDest_Output), .clk(CLK));  // open: en, clr
  Register #(.width(1)) register_13 (.D(BEQ_In), .Q(BEQ_Output), .clk(CLK));  // open: en, clr
  Register #(.width(1)) register_14 (.D(MemWrite_In), .Q(MemWrite_Output), .clk(CLK));  // open: en, clr
  Register #(.width(1)) register_15 (.D(MemRead_In), .Q(MemRead_Output), .clk(CLK));  // open: en, clr
  Register #(.width(1)) register_16 (.D(MemToReg_In), .Q(MemToReg_Output), .clk(CLK));  // open: en, clr
  Register #(.width(1)) register_17 (.D(RegWrite_In), .Q(RegWrite_Output), .clk(CLK));  // open: en, clr
  Register #(.width(1)) register_18 (.D(BNEQ_In), .Q(BNEQ_Output), .clk(CLK));  // open: en, clr
  Register #(.width(1)) register_19 (.D(AluSrc_In), .Q(AluSrc_Output), .clk(CLK));  // open: en, clr
  Register #(.width(1)) register_20 (.D(ExtOp_In), .Q(ExtOp_Output), .clk(CLK));  // open: en, clr
endmodule

module byte_extender (
  input  [15:0] Imm,
  input  lbu,
  output [15:0] out
);

  wire [15:0] bit_extender_1_out, bit_extender_2_out;

  assign bit_extender_1_out = {{8{Imm[7]}}, Imm[7:0]};  // Bit_Extender bit_extender_1
  Multiplexer #(.width(16), .enable("false")) multiplexer_1 (
    .in0(bit_extender_1_out), .in1(bit_extender_2_out), .out(out), .sel(lbu));
  assign bit_extender_2_out = {{8{1'b0}}, Imm[7:0]};  // Bit_Extender bit_extender_2
endmodule

module forward (
  input  [2:0] Rd_mem,
  input  [2:0] Rd_wb,
  input  RegisterWrite_Men,
  input  RegisterWrite_WB,
  input  [2:0] RS,
  input  [2:0] RT,
  output [1:0] ForwardA,
  output [1:0] ForwardB
);

  wire comparator_1_eq, comparator_2_eq, comparator_3_eq, comparator_4_eq, comparator_5_eq, comparator_6_eq,
       comparator_7_eq, comparator_8_eq, comparator_9_eq, not_1_out, not_2_out, not_3_out, not_4_out,
       not_5_out;
  wire [0:0] and_3_out, and_4_out;
  wire [1:1] and_1_out, and_2_out;

  not not_1 (not_1_out, comparator_1_eq);
  and and_1 (and_1_out[1], RegisterWrite_Men, not_1_out, comparator_2_eq);
  Comparator #(.width(3)) comparator_1 (.a(3'b000), .b(Rd_mem), .eq(comparator_1_eq));  // open: gt, lt
  assign ForwardA = {and_1_out[1], 1'b0} | {1'b0, and_3_out[0]};  // OR_Gate or_1, 2 bits wide
  Comparator #(.width(3)) comparator_2 (.a(RS), .b(Rd_mem), .eq(comparator_2_eq));  // open: gt, lt
  assign ForwardB = {and_2_out[1], 1'b0} | {1'b0, and_4_out[0]};  // OR_Gate or_2, 2 bits wide
  not not_2 (not_2_out, comparator_3_eq);
  and and_2 (and_2_out[1], RegisterWrite_Men, not_2_out, comparator_4_eq);
  Comparator #(.width(3)) comparator_3 (.a(3'b000), .b(Rd_mem), .eq(comparator_3_eq));  // open: gt, lt
  Comparator #(.width(3)) comparator_4 (.a(RT), .b(Rd_mem), .eq(comparator_4_eq));  // open: gt, lt
  not not_3 (not_3_out, comparator_5_eq);
  not not_4 (not_4_out, comparator_6_eq);
  and and_3 (and_3_out[0], RegisterWrite_WB, not_3_out, not_4_out, comparator_7_eq);
  Comparator #(.width(3)) comparator_5 (.a(3'b000), .b(Rd_wb), .eq(comparator_5_eq));  // open: gt, lt
  Comparator #(.width(3)) comparator_6 (.a(Rd_mem), .b(RS), .eq(comparator_6_eq));  // open: gt, lt
  Comparator #(.width(3)) comparator_7 (.a(Rd_wb), .b(RS), .eq(comparator_7_eq));  // open: gt, lt
  not not_5 (not_5_out, comparator_8_eq);
  and and_4 (and_4_out[0], RegisterWrite_WB, comparator_5_eq, not_5_out, comparator_9_eq);
  Comparator #(.width(3)) comparator_8 (.a(Rd_mem), .b(RT), .eq(comparator_8_eq));  // open: gt, lt
  Comparator #(.width(3)) comparator_9 (.a(Rd_wb), .b(RT), .eq(comparator_9_eq));  // open: gt, lt
endmodule

module pc_control (
  input  JUMP,
  input  ZERO,
  input  BEQ,
  input  BNEQ,
  input  JR,
  input  [2:0] rs,
  output [2:0] PC
);

  wire and_2_out, and_4_out;
  wire [2:1] and_1_out;

  Multiplexer #(.width(3), .enable("false")) multiplexer_1 (
    .in0({and_1_out, JUMP}), .in1(3'b111), .out(PC), .sel(and_2_out));
  and and_1 (and_1_out[1], ZERO, BEQ);
  and and_2 (and_2_out, JR, and_4_out);
  and and_3 (and_1_out[2], ~ZERO, BNEQ);  // AND_Gate
  and and_4 (and_4_out, rs[2], rs[1], rs[0]);
endmodule

module execution_buffer (
  input  [2:0] in_1,
  input  [15:0] Alu_Result_In,
  input  [15:0] in_3,
  input  MemWrite_In,
  input  MemRead_In,
  input  MemToReg_In,
  input  RegWrite_In,
  input  CLK,
  output [2:0] out_9,
  output [15:0] Alu_Result_Output,
  output [15:0] out_11,
  output out_12,
  output out_13,
  output out_14,
  output out_15
);

  Register #(.width(3)) register_1 (.D(in_1), .Q(out_9), .clk(CLK));  // open: en, clr
  Register #(.width(16)) register_2 (.D(Alu_Result_In), .Q(Alu_Result_Output), .clk(CLK));  // open: en, clr
  Register #(.width(16)) register_3 (.D(in_3), .Q(out_11), .clk(CLK));  // open: en, clr
  Register #(.width(1)) register_4 (.D(MemWrite_In), .Q(out_12), .clk(CLK));  // open: en, clr
  Register #(.width(1)) register_5 (.D(MemRead_In), .Q(out_13), .clk(CLK));  // open: en, clr
  Register #(.width(1)) register_6 (.D(MemToReg_In), .Q(out_14), .clk(CLK));  // open: en, clr
  Register #(.width(1)) register_7 (.D(RegWrite_In), .Q(out_15), .clk(CLK));  // open: en, clr
endmodule

module memory_buffer (
  input  [2:0] in_1,
  input  [15:0] AluResult_In,
  input  [15:0] MemResult_In,
  input  MemToReg_In,
  input  RegWrite_In,
  input  CLK,
  output [2:0] out_7,
  output [15:0] AluResult_Output,
  output [15:0] MemResult_Output,
  output out_10,
  output out_11
);

  Register #(.width(3)) register_1 (.D(in_1), .Q(out_7), .clk(CLK));  // open: en, clr
  Register #(.width(16)) register_2 (.D(AluResult_In), .Q(AluResult_Output), .clk(CLK));  // open: en, clr
  Register #(.width(16)) register_3 (.D(MemResult_In), .Q(MemResult_Output), .clk(CLK));  // open: en, clr
  Register #(.width(1)) register_4 (.D(MemToReg_In), .Q(out_10), .clk(CLK));  // open: en, clr
  Register #(.width(1)) register_5 (.D(RegWrite_In), .Q(out_11), .clk(CLK));  // open: en, clr
endmodule
